// Logisim project SynthBite16.circ as structural Verilog: 1 circuit, main circuit main
module main (
);

  wire AC_p1, AC_p2, AC_p3, AC_p5, AC_p18, AC_p19, AC_p20, AC_p21, AC_p22, AC_p23, AC_p24, AC_p25, AC_p26,
       AC_p27, AC_p28, AC_p29, dipswitch_1_p1, dipswitch_1_p2, dipswitch_1_p3, dipswitch_1_p4,
       dipswitch_1_p5, dipswitch_1_p6, dipswitch_1_p7, dipswitch_1_p8, MasterClock_out, undriven, undriven_2,
       undriven_3, undriven_4, undriven_5, undriven_7, undriven_8;
  wire [11:0] undriven_6;
  wire [15:0] INSTRN_data;

  Clock MasterClock (.out(MasterClock_out));
  LED led_1 (.in(MasterClock_out));
  // DipSwitch dipswitch_1: pin names not known; wires that end beside it: dipswitch_1_p1, dipswitch_1_p2, dipswitch_1_p3, dipswitch_1_p4, dipswitch_1_p5, dipswitch_1_p6, dipswitch_1_p7, dipswitch_1_p8
  // Shift_Register #(.length(16)) AC: pin names not known; wires that end beside it: AC_p1, AC_p2, AC_p3, MasterClock_out, AC_p5, dipswitch_1_p1, dipswitch_1_p2, dipswitch_1_p3, dipswitch_1_p4, dipswitch_1_p5, dipswitch_1_p6, dipswitch_1_p7, dipswitch_1_p8, dipswitch_1_p1, dipswitch_1_p2, dipswitch_1_p3, dipswitch_1_p4, AC_p18, AC_p19, AC_p20, AC_p21, AC_p22, AC_p23, AC_p24, AC_p25, AC_p26, AC_p27, AC_p28, AC_p29
  assign dipswitch_1_p1 = undriven_5 ? AC_p18 : 1'bz;  // Controlled_Buffer controlled_buffer_1
  assign dipswitch_1_p2 = undriven_5 ? AC_p19 : 1'bz;  // Controlled_Buffer controlled_buffer_2
  assign dipswitch_1_p3 = undriven_5 ? AC_p20 : 1'bz;  // Controlled_Buffer controlled_buffer_3
  assign dipswitch_1_p4 = undriven_5 ? AC_p21 : 1'bz;  // Controlled_Buffer controlled_buffer_4
  assign dipswitch_1_p5 = undriven_5 ? AC_p22 : 1'bz;  // Controlled_Buffer controlled_buffer_5
  assign dipswitch_1_p6 = undriven_5 ? AC_p23 : 1'bz;  // Controlled_Buffer controlled_buffer_6
  assign dipswitch_1_p7 = undriven_5 ? AC_p24 : 1'bz;  // Controlled_Buffer controlled_buffer_7
  assign dipswitch_1_p8 = undriven_5 ? AC_p25 : 1'bz;  // Controlled_Buffer controlled_buffer_8
  assign dipswitch_1_p1 = undriven_5 ? AC_p26 : 1'bz;  // Controlled_Buffer controlled_buffer_9
  assign dipswitch_1_p2 = undriven_5 ? AC_p27 : 1'bz;  // Controlled_Buffer controlled_buffer_10
  assign dipswitch_1_p3 = undriven_5 ? AC_p28 : 1'bz;  // Controlled_Buffer controlled_buffer_11
  assign dipswitch_1_p4 = undriven_5 ? AC_p29 : 1'bz;  // Controlled_Buffer controlled_buffer_12
  assign dipswitch_1_p5 = undriven_5 ? undriven : 1'bz;  // Controlled_Buffer controlled_buffer_13
  assign dipswitch_1_p6 = undriven_5 ? undriven_2 : 1'bz;  // Controlled_Buffer controlled_buffer_14
  assign dipswitch_1_p7 = undriven_5 ? undriven_3 : 1'bz;  // Controlled_Buffer controlled_buffer_15
  assign dipswitch_1_p8 = undriven_5 ? undriven_4 : 1'bz;  // Controlled_Buffer controlled_buffer_16
  LED led_2 (.in(dipswitch_1_p1));
  LED led_3 (.in(dipswitch_1_p2));
  LED led_4 (.in(dipswitch_1_p3));
  LED led_5 (.in(dipswitch_1_p4));
  LED led_6 (.in(dipswitch_1_p5));
  LED led_7 (.in(dipswitch_1_p6));
  LED led_8 (.in(dipswitch_1_p7));
  LED led_9 (.in(dipswitch_1_p8));
  LED led_10 (.in(dipswitch_1_p1));
  LED led_11 (.in(dipswitch_1_p2));
  LED led_12 (.in(dipswitch_1_p3));
  LED led_13 (.in(dipswitch_1_p4));
  LED led_14 (.in(dipswitch_1_p5));
  LED led_15 (.in(dipswitch_1_p6));
  LED led_16 (.in(dipswitch_1_p7));
  LED led_17 (.in(dipswitch_1_p8));
  ROM #(.dataWidth(32)) CNTRL_MEM ();  // open: addr, data
  RAM #(.addrWidth(12), .dataWidth(16), .databus("bidir")) INSTRN (
    .addr(undriven_6), .we(undriven_7), .oe(undriven_8), .clk(MasterClock_out), .data(INSTRN_data));

  // Notes on the sheet:
  //   CLOCK
  //   SYSTEM BUS
  //   16 LINES
  //   ACCUMULATOR
  //   CONTROL UNIT
  //   CONTROL MEMORY
  //   ACC BUS ON
  //   ACC RESET ASYNC
  //   ACC RESET ASYNC
  //   ACC PARALLEL LOAD
  //   ACC PARALLEL LOAD
  //   ACC SHIFT
  //   ACC SHIFT
  //   ACC SERIAL IN
  //   ACC SERIAL IN
  //   INSTRUCTIONS
endmodule
